# Fritzing sketch Learning_Circuit_Arduino (saved by Fritzing 0.9.3b)
perfboards: 1

parts:
  Part1 = Arduino Leonardo (Rev3b)
  LED3 = LED - 5mm [color="Green (560nm)" package="5 mm [THT]"]
  LED4 = LED - 5mm [color="Red (633nm)" package="5 mm [THT]"]
  LED2 = LED - 5mm [color="Yellow (595nm)" package="5 mm [THT]"]
  LED5 = LED - 5mm [color="Green (560nm)" package="5 mm [THT]"]
  R1 = Resistor [tolerance=±5% resistance=220 package=THT]
  R3 = Resistor [tolerance=±5% resistance=220 package=THT]
  R4 = Resistor [tolerance=±5% resistance=220 package=THT]
  LED1 = LED - 5mm [color="Red (633nm)" package="5 mm [THT]"]
  R6 = Trimmer Potentiometer [maximum_resistance=10kΩ package=THT]
  T1 = LM35 Temperature Sensor [package="TO92 [THT]"]
  R8 = Photocell (LDR) [package=THT]
  R9 = Resistor [tolerance=±5% resistance=10k package=THT]
  R2 = Resistor [tolerance=±5% resistance=220 package=THT]
  R10 = Resistor [tolerance=±5% resistance=220 package=THT]
  R11 = Resistor [tolerance=±5% resistance=2.2k package=THT]

nets:
  N1: Part1.D2/SDA, Part1.SDA, LED1.anode
  N2: Part1.D3_PWM/SCL, Part1.SCL, LED2.anode
  N3: Part1.D4/A6, LED3.anode
  N4: Part1.D5_PWM, LED4.anode
  N5: Part1.D6_PWM/A7, LED5.anode
  N6: Part1.3V3, R6.leg1, R8.pin_1
  N7: Part1.5V, T1.+Vs
  GND: Part1.GND, R1.Pin_1, R3.Pin_1, R4.Pin_1, R6.leg2, T1.GND, R9.Pin_1, R2.Pin_1, R10.Pin_1, R11.Pin_0, R11.Pin_1
  N8: Part1.A0, R6.wiper
  N9: Part1.A1, R8.pin_0, R9.Pin_0
  N10: Part1.A2, T1.Vout
  N11: LED3.cathode, R3.Pin_0
  N12: LED4.cathode, R4.Pin_0
  N13: LED2.cathode, R2.Pin_0
  N14: LED5.cathode, R10.Pin_0
  N15: R1.Pin_0, LED1.cathode
